# Fritzing sketch blink2 (saved by Fritzing 0.9.3b)
breadboards: 1

parts:
  VCC1 = Battery block 9V
  R2 = Resistor [tolerance=±5% resistance=10k package="0603 [SMD]"]
  R3 = Resistor [tolerance=±5% resistance=1k package="0603 [SMD]"]
  LED1 = smd LED [color="White (8000K)" package="0603 [SMD]"]
  C1 = Electrolytic Capacitor [capacitance=5µF package="0807 [SMD, electrolytic]"]
  Q1 = NPN-Transistor [package="TO92 [THT]"]
  C2 = Electrolytic Capacitor [capacitance=100μF package="0807 [SMD, electrolytic]"]
  R1 = Resistor [tolerance=±5% resistance=100k package="0603 [SMD]"]
  Q2 = PNP-Transistor [package="TO92 [THT]"]

nets:
  N1: VCC1.-, LED1.cathode, Q1.E, C2.-
  N2: VCC1.+, R2.Pin_0, C2.+, Q2.E
  N3: R2.Pin_1, R1.Pin_0
  N4: R3.Pin_0, Q2.B
  N5: R3.Pin_1, Q1.C
  N6: LED1.anode, C1.+, Q2.C
  N7: C1.-, Q1.B, R1.Pin_1
