# Fritzing sketch blink2-step2 (saved by Fritzing 0.9.3b)
breadboards: 1

parts:
  R2 = Resistor [tolerance=±5% resistance=10k package="0603 [SMD]"]
  R1 = Resistor [tolerance=±5% resistance=100k package="0603 [SMD]"]

nets:
  N1: R2.Pin_1, R1.Pin_0
