# Fritzing sketch blink2-step3 (saved by Fritzing 0.9.3b)
breadboards: 1

parts:
  R2 = Resistor [tolerance=±5% resistance=10k package="0603 [SMD]"]
  R3 = Resistor [tolerance=±5% resistance=1k package="0603 [SMD]"]
  C1 = Electrolytic Capacitor [capacitance=5µF package="0807 [SMD, electrolytic]"]
  Q1 = NPN-Transistor [package="TO92 [THT]"]
  R1 = Resistor [tolerance=±5% resistance=100k package="0603 [SMD]"]

nets:
  N1: R2.Pin_1, R1.Pin_0
  N2: R3.Pin_1, Q1.C
  N3: C1.-, Q1.B, R1.Pin_1
