# Fritzing sketch blink2-step4 (saved by Fritzing 0.9.3b)
breadboards: 2

parts:
  R2 = Resistor [tolerance=±5% resistance=10k package="0603 [SMD]"]
  R3 = Resistor [tolerance=±5% resistance=1k package="0603 [SMD]"]
  LED1 = smd LED [color="White (8000K)" package="0603 [SMD]"]  # not connected
  C1 = Electrolytic Capacitor [capacitance=5µF package="0807 [SMD, electrolytic]"]
  Q1 = NPN-Transistor [package="TO92 [THT]"]
  R1 = Resistor [tolerance=±5% resistance=100k package="0603 [SMD]"]
  Q3 = NPN-Transistor [package="TO92 [THT]"]
  R4 = Resistor [tolerance=±5% resistance=10k package="0603 [SMD]"]
  R5 = Resistor [tolerance=±5% resistance=1k package="0603 [SMD]"]
  LED2 = smd LED [color="White (8000K)" package="0603 [SMD]"]  # not connected
  C3 = Electrolytic Capacitor [capacitance=5µF package="0807 [SMD, electrolytic]"]
  R6 = Resistor [tolerance=±5% resistance=100k package="0603 [SMD]"]

nets:
  N1: R2.Pin_1, R1.Pin_0
  N2: R3.Pin_1, Q1.C
  N3: C1.-, Q1.B, R1.Pin_1
  N4: Q3.B, C3.-, R6.Pin_1
  N5: Q3.C, R5.Pin_1
  N6: R4.Pin_1, R6.Pin_0
