# Fritzing sketch blink2-step6 (saved by Fritzing 0.9.3b)
breadboards: 2

parts:
  R2 = Resistor [tolerance=±5% resistance=10k package="0603 [SMD]"]
  R3 = Resistor [tolerance=±5% resistance=1k package="0603 [SMD]"]
  LED1 = smd LED [color="White (8000K)" package="0603 [SMD]"]
  C1 = Electrolytic Capacitor [capacitance=5µF package="0807 [SMD, electrolytic]"]
  Q1 = NPN-Transistor [package="TO92 [THT]"]
  C2 = Electrolytic Capacitor [capacitance=100μF package="0807 [SMD, electrolytic]"]
  R1 = Resistor [tolerance=±5% resistance=100k package="0603 [SMD]"]
  Q2 = PNP-Transistor [package="TO92 [THT]"]
  Q3 = NPN-Transistor [package="TO92 [THT]"]
  R4 = Resistor [tolerance=±5% resistance=10k package="0603 [SMD]"]
  R5 = Resistor [tolerance=±5% resistance=1k package="0603 [SMD]"]
  LED2 = smd LED [color="White (8000K)" package="0603 [SMD]"]
  C3 = Electrolytic Capacitor [capacitance=5µF package="0807 [SMD, electrolytic]"]
  C4 = Electrolytic Capacitor [capacitance=100μF package="0807 [SMD, electrolytic]"]
  Q4 = PNP-Transistor [package="TO92 [THT]"]
  R6 = Resistor [tolerance=±5% resistance=100k package="0603 [SMD]"]

nets:
  N1: R2.Pin_1, R1.Pin_0
  N2: R3.Pin_0, Q2.B
  N3: R3.Pin_1, Q1.C
  N4: LED1.cathode, C2.-
  N5: LED1.anode, Q2.C
  N6: C1.-, Q1.B, R1.Pin_1
  N7: Q3.B, C3.-, R6.Pin_1
  N8: Q3.C, R5.Pin_1
  N9: R4.Pin_1, R6.Pin_0
  N10: R5.Pin_0, Q4.B
  N11: LED2.cathode, C4.-
  N12: LED2.anode, Q4.C
