# Fritzing sketch blink2-step7 (saved by Fritzing 0.9.3b)
breadboards: 10

parts:
  Q6 = NPN-Transistor [part_number=2N3904 package="TO92 [THT]"]
  R8 = Resistor [tolerance=±5% resistance=10k package="0603 [SMD]"]
  R10 = Resistor [tolerance=±5% resistance=1k package="0603 [SMD]"]
  LED4 = smd LED [color="Yellow (595nm)" package="0603 [SMD]"]
  C6 = Electrolytic Capacitor [capacitance=5µF package="0807 [SMD, electrolytic]"]
  C8 = Electrolytic Capacitor [capacitance=100μF package="0807 [SMD, electrolytic]"]
  Q8 = PNP-Transistor [part_number=2N3906 package="TO92 [THT]"]
  R12 = Resistor [tolerance=±5% resistance=100k package="0603 [SMD]"]
  Q10 = NPN-Transistor [part_number=2N3904 package="TO92 [THT]"]
  R14 = Resistor [tolerance=±5% resistance=10k package="0603 [SMD]"]
  R16 = Resistor [tolerance=±5% resistance=1k package="0603 [SMD]"]
  LED6 = smd LED [color="Yellow (595nm)" package="0603 [SMD]"]
  C10 = Electrolytic Capacitor [capacitance=5µF package="0807 [SMD, electrolytic]"]
  C12 = Electrolytic Capacitor [capacitance=100μF package="0807 [SMD, electrolytic]"]
  Q12 = PNP-Transistor [part_number=2N3906 package="TO92 [THT]"]
  R18 = Resistor [tolerance=±5% resistance=100k package="0603 [SMD]"]
  Q14 = NPN-Transistor [part_number=2N3904 package="TO92 [THT]"]
  R20 = Resistor [tolerance=±5% resistance=10k package="0603 [SMD]"]
  R22 = Resistor [tolerance=±5% resistance=1k package="0603 [SMD]"]
  LED8 = smd LED [color="Yellow (595nm)" package="0603 [SMD]"]
  C14 = Electrolytic Capacitor [capacitance=5µF package="0807 [SMD, electrolytic]"]
  Q16 = PNP-Transistor [part_number=2N3906 package="TO92 [THT]"]
  R24 = Resistor [tolerance=±5% resistance=100k package="0603 [SMD]"]
  Q18 = NPN-Transistor [part_number=2N3904 package="TO92 [THT]"]
  R26 = Resistor [tolerance=±5% resistance=10k package="0603 [SMD]"]
  R28 = Resistor [tolerance=±5% resistance=1k package="0603 [SMD]"]
  LED10 = smd LED [color="Yellow (595nm)" package="0603 [SMD]"]  # not connected
  C16 = Electrolytic Capacitor [capacitance=5µF package="0807 [SMD, electrolytic]"]
  R30 = Resistor [tolerance=±5% resistance=100k package="0603 [SMD]"]
  Q19 = NPN-Transistor [part_number=2N3904 package="TO92 [THT]"]
  R31 = Resistor [tolerance=±5% resistance=10k package="0603 [SMD]"]
  R32 = Resistor [tolerance=±5% resistance=1k package="0603 [SMD]"]
  C17 = Electrolytic Capacitor [capacitance=5µF package="0807 [SMD, electrolytic]"]
  R33 = Resistor [tolerance=±5% resistance=100k package="0603 [SMD]"]
  R34 = Resistor [tolerance=±5% resistance=10k package="0603 [SMD]"]
  R35 = Resistor [tolerance=±5% resistance=100k package="0603 [SMD]"]
  Q24 = NPN-Transistor [part_number=2N3904 package="TO92 [THT]"]
  R42 = Resistor [tolerance=±5% resistance=10k package="0603 [SMD]"]
  R43 = Resistor [tolerance=±5% resistance=1k package="0603 [SMD]"]
  LED13 = smd LED [color="Yellow (595nm)" package="0603 [SMD]"]  # not connected
  C22 = Electrolytic Capacitor [capacitance=5µF package="0807 [SMD, electrolytic]"]
  R44 = Resistor [tolerance=±5% resistance=100k package="0603 [SMD]"]
  Q25 = NPN-Transistor [part_number=2N3904 package="TO92 [THT]"]
  R45 = Resistor [tolerance=±5% resistance=10k package="0603 [SMD]"]
  R46 = Resistor [tolerance=±5% resistance=1k package="0603 [SMD]"]
  LED14 = smd LED [color="Yellow (595nm)" package="0603 [SMD]"]
  C23 = Electrolytic Capacitor [capacitance=5µF package="0807 [SMD, electrolytic]"]
  C24 = Electrolytic Capacitor [capacitance=100μF package="0807 [SMD, electrolytic]"]
  Q26 = PNP-Transistor [part_number=2N3906 package="TO92 [THT]"]
  R47 = Resistor [tolerance=±5% resistance=100k package="0603 [SMD]"]
  Q27 = NPN-Transistor [part_number=2N3904 package="TO92 [THT]"]
  R48 = Resistor [tolerance=±5% resistance=10k package="0603 [SMD]"]
  R49 = Resistor [tolerance=±5% resistance=1k package="0603 [SMD]"]
  LED15 = smd LED [color="Yellow (595nm)" package="0603 [SMD]"]
  C25 = Electrolytic Capacitor [capacitance=5µF package="0807 [SMD, electrolytic]"]
  C26 = Electrolytic Capacitor [capacitance=100μF package="0807 [SMD, electrolytic]"]
  Q28 = PNP-Transistor [part_number=2N3906 package="TO92 [THT]"]
  R50 = Resistor [tolerance=±5% resistance=100k package="0603 [SMD]"]
  Q29 = NPN-Transistor [part_number=2N3904 package="TO92 [THT]"]
  R51 = Resistor [tolerance=±5% resistance=10k package="0603 [SMD]"]
  R52 = Resistor [tolerance=±5% resistance=1k package="0603 [SMD]"]
  LED16 = smd LED [color="Yellow (592nm)" package="0603 [SMD]"]
  C27 = Electrolytic Capacitor [capacitance=5µF package="0807 [SMD, electrolytic]"]
  C28 = Electrolytic Capacitor [capacitance=100μF package="0807 [SMD, electrolytic]"]
  Q30 = PNP-Transistor [part_number=2N3906 package="TO92 [THT]"]
  R53 = Resistor [tolerance=±5% resistance=100k package="0603 [SMD]"]
  VCC1 = Battery block 9V

nets:
  N1: Q6.E, LED4.cathode, C8.-
  N2: Q6.B, C6.-, R12.Pin_1
  N3: Q6.C, R10.Pin_1
  N4: R8.Pin_0, C8.+, Q8.E
  N5: R8.Pin_1, R12.Pin_0
  N6: R10.Pin_0, Q8.B
  N7: LED4.anode, Q8.C
  N8: Q10.B, C10.-, R18.Pin_1
  N9: Q10.C, R16.Pin_1
  N10: R14.Pin_1, R18.Pin_0
  N11: R16.Pin_0, Q12.B
  N12: LED6.cathode, C12.-
  N13: LED6.anode, Q12.C
  N14: Q14.B, C14.-, R24.Pin_1
  N15: Q14.C, R22.Pin_1
  N16: R20.Pin_1, R24.Pin_0
  N17: R22.Pin_0, Q16.B
  N18: LED8.anode, Q16.C
  N19: Q18.B, C16.-, R30.Pin_1
  N20: Q18.C, R28.Pin_1
  N21: R26.Pin_1, R30.Pin_0
  N22: Q19.B, C17.-, R33.Pin_1
  N23: Q19.C, R32.Pin_1
  N24: R31.Pin_1, R33.Pin_0
  N25: R34.Pin_1, R35.Pin_0
  N26: Q24.B, C22.-, R44.Pin_1
  N27: Q24.C, R43.Pin_1
  N28: R42.Pin_1, R44.Pin_0
  N29: Q25.B, C23.-, R47.Pin_1
  N30: Q25.C, R46.Pin_1
  N31: R45.Pin_1, R47.Pin_0
  N32: R46.Pin_0, Q26.B
  N33: LED14.cathode, C24.-
  N34: LED14.anode, Q26.C
  N35: Q27.E, LED15.cathode, C26.-
  N36: Q27.B, C25.-, R50.Pin_1
  N37: Q27.C, R49.Pin_1
  N38: R48.Pin_0, C26.+, Q28.E
  N39: R48.Pin_1, R50.Pin_0
  N40: R49.Pin_0, Q28.B
  N41: LED15.anode, C25.+, Q28.C
  N42: Q29.E, LED16.cathode, C28.-, VCC1.-
  N43: Q29.B, C27.-, R53.Pin_1
  N44: Q29.C, R52.Pin_1
  N45: R51.Pin_0, C28.+, Q30.E, VCC1.+
  N46: R51.Pin_1, R53.Pin_0
  N47: R52.Pin_0, Q30.B
  N48: LED16.anode, C27.+, Q30.C
