# Fritzing sketch tick (saved by Fritzing 0.9.3b)
breadboards: 1

parts:
  VCC1 = Battery block 9V
  R6 = Resistor [tolerance=±5% resistance=10k package="0603 [SMD]"]
  R7 = Resistor [tolerance=±5% resistance=1k package="0603 [SMD]"]
  C3 = Electrolytic Capacitor [capacitance=5µF package="0807 [SMD, electrolytic]"]
  Q4 = NPN-Transistor [package="TO92 [THT]"]
  Q5 = PNP-Transistor [package="TO92 [THT]"]
  C5 = Electrolytic Capacitor [capacitance=100μF package="0807 [SMD, electrolytic]"]
  R8 = Resistor [tolerance=±5% resistance=100k package="0603 [SMD]"]
  J1 = Piezo Speaker

nets:
  N1: VCC1.-, Q4.E, C5.-, J1.pin1
  N2: VCC1.+, R6.Pin_0, Q5.E, C5.+
  N3: R6.Pin_1, R8.Pin_0
  N4: R7.Pin_0, Q5.B
  N5: R7.Pin_1, Q4.C
  N6: C3.-, Q4.B, R8.Pin_1
  N7: C3.+, Q5.C, J1.pin2
