# Fritzing sketch multivibrator-LED (saved by Fritzing 0.9.3b)
breadboards: 1

parts:
  R3 = Resistor [tolerance=±5% resistance=470 package="0603 [SMD]"]
  R4 = Resistor [tolerance=±5% resistance=10k package="0603 [SMD]"]
  LED2 = smd LED [color="White (8000K)" package="0603 [SMD]"]
  C1 = Electrolytic Capacitor [capacitance=10nF package="0807 [SMD, electrolytic]"]
  U1 = TRANSISTOR_NPN_2 [package=to-92]
  R5 = Resistor [tolerance=±5% resistance=10k package="0603 [SMD]"]
  R6 = Resistor [tolerance=±5% resistance=470 package="0603 [SMD]"]
  LED3 = smd LED [color="White (8000K)" package="0603 [SMD]"]
  C2 = Electrolytic Capacitor [capacitance=10nF package="0807 [SMD, electrolytic]"]
  U2 = TRANSISTOR_NPN_2 [package=to-92]

nets:
  N1: R3.Pin_0, C1.-, U2.B
  N2: R3.Pin_1, R4.Pin_1, R5.Pin_1, R6.Pin_1
  N3: R4.Pin_0, LED2.anode
  N4: LED2.cathode, C1.+, U1.C
  N5: U1.B, R6.Pin_0, C2.-
  N6: U1.E, U2.E
  N7: R5.Pin_0, LED3.anode
  N8: LED3.cathode, C2.+, U2.C
