# Fritzing sketch multivibrator-LED3 (saved by Fritzing 0.9.3b)
breadboards: 1

parts:
  R5 = Resistor [tolerance=±5% resistance=10k package="0603 [SMD]"]
  R6 = Resistor [tolerance=±5% resistance=10k package="0603 [SMD]"]
  R7 = Resistor [tolerance=±5% resistance=470 package="0603 [SMD]"]
  R8 = Resistor [tolerance=±5% resistance=470 package="0603 [SMD]"]
  LED2 = smd LED [color="White (8000K)" package="0603 [SMD]"]
  LED1 = smd LED [color="White (8000K)" package="0603 [SMD]"]
  C3 = Electrolytic Capacitor [capacitance=10µF package="0807 [SMD, electrolytic]"]
  C4 = Electrolytic Capacitor [capacitance=10µF package="0807 [SMD, electrolytic]"]
  Q3 = NPN-Transistor [package="TO92 [THT]"]
  Q4 = NPN-Transistor [package="TO92 [THT]"]
  VCC1 = Battery block 9V

nets:
  N1: R5.Pin_0, R6.Pin_0, R7.Pin_0, R8.Pin_0, VCC1.+
  N2: R5.Pin_1, C3.-, Q4.B
  N3: R6.Pin_1, C4.-, Q3.B
  N4: R7.Pin_1, LED1.anode
  N5: R8.Pin_1, LED2.anode
  N6: LED2.cathode, C3.+, Q3.C
  N7: LED1.cathode, C4.+, Q4.C
  N8: Q3.E, Q4.E, VCC1.-
