# Fritzing sketch multivibrator-LED3-steps (saved by Fritzing 0.9.3b)
breadboards: 8

parts:
  R9 = Resistor [tolerance=±5% resistance=10k package="0603 [SMD]"]
  R10 = Resistor [tolerance=±5% resistance=10k package="0603 [SMD]"]
  R11 = Resistor [tolerance=±5% resistance=470 package="0603 [SMD]"]
  R12 = Resistor [tolerance=±5% resistance=470 package="0603 [SMD]"]
  LED3 = smd LED [color="White (8000K)" package="0603 [SMD]"]  # not connected
  LED4 = smd LED [color="White (8000K)" package="0603 [SMD]"]  # not connected
  R13 = Resistor [tolerance=±5% resistance=10k package="0603 [SMD]"]
  R14 = Resistor [tolerance=±5% resistance=10k package="0603 [SMD]"]
  R15 = Resistor [tolerance=±5% resistance=10k package="0603 [SMD]"]
  R16 = Resistor [tolerance=±5% resistance=10k package="0603 [SMD]"]
  R17 = Resistor [tolerance=±5% resistance=470 package="0603 [SMD]"]
  R18 = Resistor [tolerance=±5% resistance=470 package="0603 [SMD]"]
  R19 = Resistor [tolerance=±5% resistance=470 package="0603 [SMD]"]
  R20 = Resistor [tolerance=±5% resistance=470 package="0603 [SMD]"]
  LED6 = smd LED [color="White (8000K)" package="0603 [SMD]"]
  LED8 = smd LED [color="White (8000K)" package="0603 [SMD]"]
  VCC8 = Battery block 9V
  Q12 = NPN-Transistor [package="TO92 [THT]"]  # not connected
  Q13 = NPN-Transistor [package="TO92 [THT]"]
  Q14 = NPN-Transistor [package="TO92 [THT]"]
  Q16 = NPN-Transistor [package="TO92 [THT]"]
  Q17 = NPN-Transistor [package="TO92 [THT]"]  # not connected
  Q18 = NPN-Transistor [package="TO92 [THT]"]
  R21 = Resistor [tolerance=±5% resistance=10k package="0603 [SMD]"]
  R22 = Resistor [tolerance=±5% resistance=10k package="0603 [SMD]"]
  R23 = Resistor [tolerance=±5% resistance=10k package="0603 [SMD]"]
  R24 = Resistor [tolerance=±5% resistance=10k package="0603 [SMD]"]
  R25 = Resistor [tolerance=±5% resistance=10k package="0603 [SMD]"]
  R26 = Resistor [tolerance=±5% resistance=10k package="0603 [SMD]"]
  R27 = Resistor [tolerance=±5% resistance=10k package="0603 [SMD]"]
  R28 = Resistor [tolerance=±5% resistance=10k package="0603 [SMD]"]
  R29 = Resistor [tolerance=±5% resistance=470 package="0603 [SMD]"]
  R30 = Resistor [tolerance=±5% resistance=470 package="0603 [SMD]"]
  R31 = Resistor [tolerance=±5% resistance=470 package="0603 [SMD]"]
  R32 = Resistor [tolerance=±5% resistance=470 package="0603 [SMD]"]
  R33 = Resistor [tolerance=±5% resistance=470 package="0603 [SMD]"]
  R34 = Resistor [tolerance=±5% resistance=470 package="0603 [SMD]"]
  R35 = Resistor [tolerance=±5% resistance=470 package="0603 [SMD]"]
  R36 = Resistor [tolerance=±5% resistance=470 package="0603 [SMD]"]
  LED9 = smd LED [color="White (8000K)" package="0603 [SMD]"]
  LED10 = smd LED [color="White (8000K)" package="0603 [SMD]"]
  LED11 = smd LED [color="White (8000K)" package="0603 [SMD]"]
  LED12 = smd LED [color="White (8000K)" package="0603 [SMD]"]
  LED13 = smd LED [color="White (8000K)" package="0603 [SMD]"]
  LED14 = smd LED [color="White (8000K)" package="0603 [SMD]"]
  LED15 = smd LED [color="White (8000K)" package="0603 [SMD]"]
  LED16 = smd LED [color="White (8000K)" package="0603 [SMD]"]
  C11 = Electrolytic Capacitor [capacitance=10µF package="0807 [SMD, electrolytic]"]
  C12 = Electrolytic Capacitor [capacitance=10µF package="0807 [SMD, electrolytic]"]
  C13 = Electrolytic Capacitor [capacitance=10µF package="0807 [SMD, electrolytic]"]
  C14 = Electrolytic Capacitor [capacitance=10µF package="0807 [SMD, electrolytic]"]
  C15 = Electrolytic Capacitor [capacitance=10µF package="0807 [SMD, electrolytic]"]
  C16 = Electrolytic Capacitor [capacitance=10µF package="0807 [SMD, electrolytic]"]
  C17 = Electrolytic Capacitor [capacitance=10µF package="0807 [SMD, electrolytic]"]
  C18 = Electrolytic Capacitor [capacitance=10µF package="0807 [SMD, electrolytic]"]
  R37 = Resistor [tolerance=±5% resistance=10k package="0603 [SMD]"]
  R38 = Resistor [tolerance=±5% resistance=10k package="0603 [SMD]"]
  R39 = Resistor [tolerance=±5% resistance=470 package="0603 [SMD]"]
  R40 = Resistor [tolerance=±5% resistance=470 package="0603 [SMD]"]
  LED17 = smd LED [color="White (8000K)" package="0603 [SMD]"]
  C19 = Electrolytic Capacitor [capacitance=10µF package="0807 [SMD, electrolytic]"]
  C20 = Electrolytic Capacitor [capacitance=10µF package="0807 [SMD, electrolytic]"]
  LED19 = smd LED [color="White (8000K)" package="0603 [SMD]"]

nets:
  N1: R9.Pin_0, R10.Pin_0, R11.Pin_0, R12.Pin_0
  N2: R13.Pin_0, R15.Pin_0, R17.Pin_0, R19.Pin_0
  N3: R14.Pin_0, R16.Pin_0, R18.Pin_0, R20.Pin_0
  N4: R18.Pin_1, LED8.anode
  N5: R20.Pin_1, LED6.anode
  N6: VCC8.-, Q13.E, Q18.E
  N7: VCC8.+, R23.Pin_0, R26.Pin_0, R31.Pin_0, R34.Pin_0
  N8: Q13.B, R23.Pin_1, C14.-
  N9: Q13.C, LED15.cathode, C16.+
  N10: Q14.E, Q16.E
  N11: Q14.C, LED14.cathode, C17.+
  N12: Q16.C, LED10.cathode, C12.+
  N13: Q18.B, R26.Pin_1, C16.-
  N14: Q18.C, LED11.cathode, C14.+
  N15: R21.Pin_0, R25.Pin_0, R29.Pin_0, R33.Pin_0
  N16: R21.Pin_1, C11.-
  N17: R22.Pin_0, R28.Pin_0, R30.Pin_0, R35.Pin_0
  N18: R22.Pin_1, C13.-
  N19: R24.Pin_0, R27.Pin_0, R32.Pin_0, R36.Pin_0
  N20: R24.Pin_1, C12.-
  N21: R25.Pin_1, C15.-
  N22: R27.Pin_1, C17.-
  N23: R28.Pin_1, C18.-
  N24: R29.Pin_1, LED13.anode
  N25: R30.Pin_1, LED16.anode
  N26: R31.Pin_1, LED15.anode
  N27: R32.Pin_1, LED14.anode
  N28: R33.Pin_1, LED9.anode
  N29: R34.Pin_1, LED11.anode
  N30: R35.Pin_1, LED12.anode
  N31: R36.Pin_1, LED10.anode
  N32: LED9.cathode, C11.+
  N33: LED12.cathode, C13.+
  N34: LED13.cathode, C15.+
  N35: LED16.cathode, C18.+
  N36: R37.Pin_0, R38.Pin_0, R39.Pin_0, R40.Pin_0
  N37: R37.Pin_1, C19.-
  N38: R38.Pin_1, C20.-
  N39: R39.Pin_1, LED19.cathode
  N40: R40.Pin_1, LED17.anode
  N41: LED17.cathode, C19.+
  N42: C20.+, LED19.anode
